// Logisim project psxcpu_cells_evo.circ as structural Verilog
module NOR_NAND (
  input  a,
  input  b,
  input  c,
  input  d,
  output x,
  output x2
);

  wire and_1_out, transistor_1_out, transistor_2_out, transistor_8_out;

  Transistor transistor_1 (.in(1'b1), .out(transistor_1_out), .gate(a));
  Transistor transistor_2 (.in(transistor_1_out), .out(transistor_2_out), .gate(b));
  Transistor transistor_3 (.in(transistor_2_out), .out(x), .gate(c));
  Transistor transistor_4 (.in(transistor_2_out), .out(x), .gate(d));
  Transistor #(.\type ("n")) transistor_5 (.in(1'b0), .out(x), .gate(a));
  Transistor #(.\type ("n")) transistor_6 (.in(1'b0), .out(x), .gate(b));
  Transistor #(.\type ("n")) transistor_7 (.in(transistor_8_out), .out(x), .gate(c));
  Transistor #(.\type ("n")) transistor_8 (.in(1'b0), .out(transistor_8_out), .gate(d));
  and and_1 (and_1_out, d, c);
  nor nor_1 (x2, and_1_out, b, a);

  // Notes on the sheet:
  //   b
  //   c
  //   a0
  //   a1
  //   211-AOI
endmodule

module NAND_NOR (
  input  a,
  input  b,
  input  c,
  input  d,
  output x,
  output x2
);

  wire or_1_out, transistor_3_out, transistor_5_out, transistor_6_out;

  Transistor transistor_1 (.in(1'b1), .out(x), .gate(a));
  Transistor transistor_2 (.in(1'b1), .out(x), .gate(b));
  Transistor transistor_3 (.in(1'b1), .out(transistor_3_out), .gate(c));
  Transistor transistor_4 (.in(transistor_3_out), .out(x), .gate(d));
  or or_1 (or_1_out, c, d);
  Transistor #(.\type ("n")) transistor_5 (.in(1'b0), .out(transistor_5_out), .gate(a));
  Transistor #(.\type ("n")) transistor_6 (.in(transistor_5_out), .out(transistor_6_out), .gate(b));
  Transistor #(.\type ("n")) transistor_7 (.in(transistor_6_out), .out(x), .gate(c));
  Transistor #(.\type ("n")) transistor_8 (.in(transistor_6_out), .out(x), .gate(d));
  nand nand_1 (x2, or_1_out, a, b);

  // Notes on the sheet:
  //   a0
  //   a1
  //   b
  //   c
  //   211-OAI
endmodule
